// Logisim project CT8.circ as structural Verilog
module main (
  input  [7:0] in_1,
  input  in_2,
  input  in_3,
  input  in_4
);

  wire alu_1_cout, AOE, AWE, C, flagreg_1_cout, undriven;
  wire [2:0] undriven_2;
  wire [3:0] Flag;
  wire [5:0] instrdecoder_1_p7;
  wire [7:0] Accumulator_dout, controlled_buffer_1_out, instrreg_1_out_5, Temp_dout;
  wire [15:0] regbank_1_addrbus;

  assign controlled_buffer_1_out = in_2 ? in_1 : 8'bz;  // Controlled_Buffer controlled_buffer_1
  // countr countr_1: pin names not known
  CLK clk_1 ();  // open: Halt, Rise, Fall, FullClock
  regs Accumulator (.Din(controlled_buffer_1_out), .WE(AWE), .Clck(C), .OE(AOE), .Dout(Accumulator_dout));  // open: Rst
  regs Temp (.Din(controlled_buffer_1_out), .WE(in_3), .Clck(C), .OE(in_4), .Dout(Temp_dout));  // open: Rst
  flagReg flagreg_1 (
    .Din(controlled_buffer_1_out), .Carryin(alu_1_cout), .WE(undriven), .Clck(C), .Dout(Flag),
    .Cout(flagreg_1_cout));  // open: Rst
  ALU alu_1 (
    .A(Accumulator_dout), .B(Temp_dout), .Cin(flagreg_1_cout), .OutEn({in_4, undriven}),
    .Dout(controlled_buffer_1_out), .COut(alu_1_cout));  // open: in_6, CEnbl
  // Probe on controlled_buffer_1_out
  instrReg instrreg_1 (.instIn(controlled_buffer_1_out), .Clck(C), .out_5(instrreg_1_out_5));  // open: WE, Rst
  // instrDecoder instrdecoder_1: pin names not known; wires that end beside it: instrdecoder_1_p7[5], instrdecoder_1_p7[4], instrdecoder_1_p7[3], instrdecoder_1_p7[2], instrdecoder_1_p7[1], instrreg_1_out_5, instrdecoder_1_p7[0]
  RegBank regbank_1 (
    .SEL(undriven_2), .Datain(controlled_buffer_1_out), .Awe(AWE), .Aoe(AOE),
    .DataOut(controlled_buffer_1_out), .AddrBus(regbank_1_addrbus));  // open: Clk, OE, WE, reset

  // Other names for the same wires on the sheet: OE = in_4
endmodule

module ALU (
  input  CEnbl,
  input  Cin,
  input  OutEn,
  input  [7:0] A,
  input  [7:0] B,
  input  [5:0] in_6,
  output SF,
  output [7:0] Dout,
  output COut
);

  wire and_1_out, or_1_out, xor_2_out;
  wire [7:0] adder_1_out, and_2_out, controlled_buffer_1_out, not_1_out, or_2_out, xor_1_out, xor_3_out;

  // Probe on A
  // Probe on B
  assign xor_1_out = B ^ {8{in_6[1]}};  // XOR_Gate xor_1, 8 bits wide
  and and_1 (and_1_out, CEnbl, Cin);
  xor xor_2 (xor_2_out, and_1_out, in_6[1]);
  or or_1 (or_1_out, in_6[1], in_6[0]);
  assign controlled_buffer_1_out = or_1_out ? adder_1_out : 8'bz;  // Controlled_Buffer controlled_buffer_1
  Adder adder_1 (.a(A), .b(xor_1_out), .out(adder_1_out), .cin(xor_2_out), .cout(COut));
  assign and_2_out = A & xor_1_out;  // AND_Gate and_2, 8 bits wide
  assign controlled_buffer_1_out = in_6[2] ? and_2_out : 8'bz;  // Controlled_Buffer controlled_buffer_2
  assign or_2_out = A | xor_1_out;  // OR_Gate or_2, 8 bits wide
  assign controlled_buffer_1_out = in_6[3] ? or_2_out : 8'bz;  // Controlled_Buffer controlled_buffer_3
  assign xor_3_out = A ^ xor_1_out;  // XOR_Gate xor_3, 8 bits wide
  assign controlled_buffer_1_out = in_6[4] ? xor_3_out : 8'bz;  // Controlled_Buffer controlled_buffer_4
  assign not_1_out = ~xor_1_out;  // NOT_Gate not_1, 8 bits wide
  assign controlled_buffer_1_out = in_6[5] ? not_1_out : 8'bz;  // Controlled_Buffer controlled_buffer_5
  assign Dout = OutEn ? controlled_buffer_1_out : 8'bz;  // Controlled_Buffer controlled_buffer_6
  // Probe on Dout

  assign SF = OutEn;
endmodule

module instrDecoder (
  input  [7:0] instr,
  output ADD_op,
  output HLT,
  output SUB_op,
  output AND_op,
  output CMP_op,
  output OR_op,
  output ALUop,
  output XOR_op,
  output NOT_op,
  output LW,
  output SW,
  output MOV,
  output JMP,
  output JZ,
  output JC,
  output NOP,
  output [2:0] REG_MUX
);

  wire and_1_out, demultiplexer_2_out1, demultiplexer_2_out6, nor_1_out, nor_2_out;

  nor nor_1 (nor_1_out, HLT, instr[3]);
  Demultiplexer #(.select(3)) demultiplexer_1 (
    .out1(LW), .out2(SW), .out3(MOV), .out4(JMP), .out5(JZ), .out6(JC), .out7(NOP), .in(nor_1_out),
    .sel(instr[2:0]));  // open: out0
  and and_1 (and_1_out, nor_2_out, instr[4]);
  assign REG_MUX = and_1_out ? instr[7:5] : 3'bz;  // Controlled_Buffer controlled_buffer_1
  and and_2 (HLT, ~instr[0], ~instr[1], ~instr[2], ~instr[3], ~instr[4], ~instr[5], ~instr[6], ~instr[7]);  // AND_Gate
  Demultiplexer #(.select(3)) demultiplexer_2 (
    .out0(ADD_op), .out1(demultiplexer_2_out1), .out2(AND_op), .out3(OR_op), .out4(XOR_op), .out5(NOT_op),
    .out6(demultiplexer_2_out6), .out7(CMP_op), .in(instr[3]), .sel(instr[2:0]));
  nor nor_2 (nor_2_out, JMP, JZ, JC);
  or or_1 (SUB_op, demultiplexer_2_out1, CMP_op);

  assign ALUop = instr[3];

  // Notes on the sheet:
  //   regImportant
  //   NoREG
endmodule

module regs (
  input  [7:0] Din,
  input  WE,
  input  Clck,
  input  Rst,
  input  OE,
  output [7:0] Dout
);

  wire [7:0] register_1_q;

  Register register_1 (.D(Din), .en(WE), .clk(Clck), .Q(register_1_q), .clr(Rst));
  assign Dout = OE ? register_1_q : 8'bz;  // Controlled_Buffer controlled_buffer_1
endmodule

module instrReg (
  input  [7:0] instIn,
  input  WE,
  input  Clck,
  input  Rst,
  output [7:0] out_5
);

  Register register_1 (.D(instIn), .en(WE), .clk(Clck), .Q(out_5), .clr(Rst));
endmodule

module flagReg (
  input  [7:0] Din,
  input  Carryin,
  input  WE,
  input  Clck,
  input  Rst,
  output [3:0] Dout,
  output Cout
);

  wire [3:3] and_1_out;

  and and_1 (and_1_out[3], ~Din[0], ~Din[1], ~Din[2], ~Din[3], ~Din[4], ~Din[5], ~Din[6], ~Din[7]);  // AND_Gate
  Register #(.width(4)) register_1 (
    .D({and_1_out[3], Din[0], Din[7], Carryin}), .en(WE), .clk(Clck), .Q({Dout[3:1], Cout}), .clr(Rst));

  assign Dout[0] = Cout;

  // Notes on the sheet:
  //   odd
  //   N
  //   Z
endmodule

module RegBank (
  input  [2:0] SEL,
  input  Clk,
  input  OE,
  input  WE,
  input  [7:0] Datain,
  input  reset,
  output Awe,
  output Aoe,
  output [7:0] DataOut,
  output [15:0] AddrBus
);

  wire decoder_1_out1, decoder_1_out2, decoder_1_out3, decoder_1_out4, decoder_1_out5, decoder_1_out6,
       decoder_2_out1, decoder_2_out2, decoder_2_out3, decoder_2_out4, decoder_2_out5, decoder_2_out6;

  Decoder #(.select(3)) decoder_1 (
    .out0(Awe), .out1(decoder_1_out1), .out2(decoder_1_out2), .out3(decoder_1_out3), .out4(decoder_1_out4),
    .out5(decoder_1_out5), .out6(decoder_1_out6), .sel(SEL), .en(WE));  // open: out7
  regs B (.Din(Datain), .WE(decoder_1_out1), .Clck(Clk), .Rst(reset), .OE(decoder_2_out1), .Dout(DataOut));
  regs D (.Din(Datain), .WE(decoder_1_out3), .Clck(Clk), .Rst(reset), .OE(decoder_2_out3), .Dout(DataOut));
  HLreg hlreg_1 (
    .reset(reset), .DinH(Datain), .clock(Clk), .Hoe(decoder_2_out6), .Loe(decoder_2_out5), .DinL(Datain),
    .Hwe(decoder_1_out6), .Lwe(decoder_1_out5), .H_out(DataOut), .Dout(AddrBus), .L_out(DataOut));
  regs C (.Din(Datain), .WE(decoder_1_out2), .Clck(Clk), .Rst(reset), .OE(decoder_2_out2), .Dout(DataOut));
  regs E (.Din(Datain), .WE(decoder_1_out4), .Clck(Clk), .Rst(reset), .OE(decoder_2_out4), .Dout(DataOut));
  Decoder #(.select(3)) decoder_2 (
    .out0(Aoe), .out1(decoder_2_out1), .out2(decoder_2_out2), .out3(decoder_2_out3), .out4(decoder_2_out4),
    .out5(decoder_2_out5), .out6(decoder_2_out6), .sel(SEL), .en(OE));  // open: out7

  // Other names for the same wires on the sheet: r = reset
endmodule

module PC (
  input  load,
  input  [15:0] AddrBusIn,
  input  PC_E,
  input  Clock,
  input  Clear,
  input  PC_OE,
  output [15:0] AddrBusOut
);

  wire [15:0] adder_1_out, multiplexer_1_out, register_1_q;

  Register #(.width(16)) register_1 (.D(multiplexer_1_out), .en(PC_E), .clk(Clock), .Q(register_1_q), .clr(Clear));
  Multiplexer #(.width(16)) multiplexer_1 (.in0(adder_1_out), .in1(AddrBusIn), .out(multiplexer_1_out), .sel(load));
  Adder #(.width(16)) adder_1 (.a(register_1_q), .b(16'h1), .out(adder_1_out), .cin(1'b0));  // open: cout
  assign AddrBusOut = PC_OE ? register_1_q : 16'bz;  // Controlled_Buffer controlled_buffer_1
endmodule

module CLK (
  input  Halt,
  output Rise,
  output Fall,
  output FullClock
);

  wire clock_1_out, not_1_out, not_2_out, not_3_out, not_4_out;

  Clock clock_1 (.out(clock_1_out));
  and and_1 (FullClock, clock_1_out, ~Halt);  // AND_Gate
  not not_1 (not_1_out, FullClock);
  and and_2 (Rise, FullClock, not_1_out);
  not not_2 (not_2_out, FullClock);
  not not_3 (not_3_out, FullClock);
  and and_3 (Fall, not_2_out, not_4_out);
  not not_4 (not_4_out, not_3_out);
endmodule

module HLreg (
  input  [7:0] DinH,
  input  Hoe,
  input  Hwe,
  input  Lwe,
  input  Loe,
  input  clock,
  input  reset,
  input  [7:0] DinL,
  output [7:0] H_out,
  output [15:0] Dout,
  output [7:0] L_out
);

  Register H (.D(DinH), .en(Hwe), .clk(clock), .Q(Dout[15:8]), .clr(reset));
  Register L (.D(DinL), .en(Lwe), .clk(clock), .Q(Dout[7:0]), .clr(reset));
  assign H_out = Hoe ? Dout[15:8] : 8'bz;  // Controlled_Buffer controlled_buffer_1
  assign L_out = Loe ? Dout[7:0] : 8'bz;  // Controlled_Buffer controlled_buffer_2
endmodule

module countr (
  input  clk,
  input  rst,
  output [1:0] out_3
);

  wire and_1_out, j_k_ff_1_qn, or_1_out;

  or or_1 (or_1_out, rst, and_1_out);
  J_K_Flip_Flop j_k_ff_1 (
    .J(1'b1), .K(1'b1), .clk(clk), .Q(out_3[0]), .Qn(j_k_ff_1_qn), .reset(or_1_out));  // open: preset
  J_K_Flip_Flop j_k_ff_2 (.J(1'b1), .K(1'b1), .clk(j_k_ff_1_qn), .Q(out_3[1]), .reset(or_1_out));  // open: Qn, preset
  and and_1 (and_1_out, out_3[0], out_3[1]);
endmodule

module ALU2 (
  input  CEnbl,
  input  Cin,
  input  [7:0] A,
  input  [7:0] B,
  input  [2:0] OP,
  input  OutEn,
  output [7:0] out_7,
  output COut,
  output Z,
  output SaveFlag,
  output N,
  output V
);

  wire adder_1_cout, and_1_out, and_3_out, decoder_1_out0, decoder_1_out2, decoder_1_out3, decoder_1_out4,
       decoder_1_out5, nor_1_out, not_2_out, or_1_out, xor_2_out, xor_4_out, xor_5_out;
  wire [7:0] adder_1_out, and_2_out, controlled_buffer_1_out, not_1_out, or_2_out, xor_1_out, xor_3_out;
  wire [7:7] decoder_1_out1;

  // Probe on A
  // Probe on B
  assign xor_1_out = B ^ {8{decoder_1_out1[7]}};  // XOR_Gate xor_1, 8 bits wide
  Decoder #(.select(3)) decoder_1 (
    .out0(decoder_1_out0), .out1(decoder_1_out1[7]), .out2(decoder_1_out2), .out3(decoder_1_out3),
    .out4(decoder_1_out4), .out5(decoder_1_out5), .sel(OP), .en(1'b1));  // open: out6, out7
  and and_1 (and_1_out, CEnbl, Cin);
  xor xor_2 (xor_2_out, and_1_out, decoder_1_out1[7]);
  or or_1 (or_1_out, decoder_1_out1[7], decoder_1_out0);
  assign controlled_buffer_1_out = or_1_out ? adder_1_out : 8'bz;  // Controlled_Buffer controlled_buffer_1
  Adder adder_1 (.a(A), .b(xor_1_out), .out(adder_1_out), .cin(xor_2_out), .cout(adder_1_cout));
  assign and_2_out = A & xor_1_out;  // AND_Gate and_2, 8 bits wide
  assign controlled_buffer_1_out = decoder_1_out2 ? and_2_out : 8'bz;  // Controlled_Buffer controlled_buffer_2
  assign or_2_out = A | xor_1_out;  // OR_Gate or_2, 8 bits wide
  assign controlled_buffer_1_out = decoder_1_out3 ? or_2_out : 8'bz;  // Controlled_Buffer controlled_buffer_3
  assign xor_3_out = A ^ xor_1_out;  // XOR_Gate xor_3, 8 bits wide
  assign controlled_buffer_1_out = decoder_1_out4 ? xor_3_out : 8'bz;  // Controlled_Buffer controlled_buffer_4
  assign not_1_out = ~xor_1_out;  // NOT_Gate not_1, 8 bits wide
  assign controlled_buffer_1_out = decoder_1_out5 ? not_1_out : 8'bz;  // Controlled_Buffer controlled_buffer_5
  xor xor_4 (xor_4_out, controlled_buffer_1_out[7], A[7]);
  xor xor_5 (xor_5_out, A[7], B[7]);
  not not_2 (not_2_out, xor_5_out);
  nor nor_1 (nor_1_out, controlled_buffer_1_out[0], controlled_buffer_1_out[1], controlled_buffer_1_out[2], controlled_buffer_1_out[3], controlled_buffer_1_out[4], controlled_buffer_1_out[5], controlled_buffer_1_out[6], controlled_buffer_1_out[7]);
  and and_3 (and_3_out, xor_4_out, not_2_out);
  assign out_7 = OutEn ? controlled_buffer_1_out : 8'bz;  // Controlled_Buffer controlled_buffer_6
  assign COut = OutEn ? adder_1_cout : 1'bz;  // Controlled_Buffer controlled_buffer_7
  assign Z = OutEn ? nor_1_out : 1'bz;  // Controlled_Buffer controlled_buffer_8
  assign N = OutEn ? controlled_buffer_1_out[7] : 1'bz;  // Controlled_Buffer controlled_buffer_9
  assign V = OutEn ? and_3_out : 1'bz;  // Controlled_Buffer controlled_buffer_10
  // Probe on out_7

  assign SaveFlag = OutEn;
endmodule
